# Fritzing sketch 7SegmentShiftRegister (saved by Fritzing 0.8.7b)
circuit board: 6.88566cm x 5.36311cm
breadboards: 1

parts:
  Part1 = Arduino Uno (Rev3)
  DI1 = 7-Segment LED Display [package=THT]
  R2 = Resistor [tolerance=±5% resistance=150 package=THT]
  R3 = Resistor [tolerance=±5% resistance=150 package=THT]
  R4 = Resistor [tolerance=±5% resistance=150 package=THT]
  R5 = Resistor [tolerance=±5% resistance=150 package=THT]
  R6 = Resistor [tolerance=±5% resistance=150 package=THT]
  R7 = Resistor [tolerance=±5% resistance=150 package=THT]
  R8 = Resistor [tolerance=±5% resistance=150 package=THT]
  C1 = Capacitor [package=cap-pth-small]
  U1 = 74HC595 [package="DIP16 [THT]"]

nets:
  N1: Part1.D2, U1.Q0
  N2: Part1.D3_PWM, U1.ST_CP
  N3: Part1.D4, U1.SH_CP
  5V: Part1.5V, C1.1, U1.MR, U1.VCC
  GND: Part1.GND, DI1.commAnode#2, C1.2, U1.GND, U1.OE
  N4: DI1.cathodeE, R6.Pin_1
  N5: DI1.cathodeD, R7.Pin_1
  N6: DI1.cathodeC, R8.Pin_0
  N7: DI1.cathodeB, R4.Pin_0
  N8: DI1.cathodeA, R5.Pin_0
  N9: DI1.cathodeF, R3.Pin_1
  N10: DI1.cathodeG, R2.Pin_1
  N11: R2.Pin_0, U1.Q5
  N12: R3.Pin_0, U1.Q6
  N13: R4.Pin_1, U1.Q1
  N14: R5.Pin_1, U1.DS
  N15: R6.Pin_0, U1.Q4
  N16: R7.Pin_0, U1.Q3
  N17: R8.Pin_1, U1.Q2
