# Fritzing sketch IRLED (saved by Fritzing 0.8.7b)
breadboards: 1

parts:
  Part1 = Arduino Uno (Rev3)
  LED1 = LED - 5mm [color="Infrared (940nm)" package="5 mm [THT]"]
  R1 = Resistor [tolerance=±5% resistance=150 package=THT]
  Q1 = LTR-301 [package=ltr-301]
  R2 = Resistor [tolerance=±5% resistance=1k package=THT]

nets:
  N1: Part1.A0, Q1.E, R2.Pin_1
  N2: Part1.GND, R1.Pin_0, R2.Pin_0
  N3: Part1.5V, LED1.anode, Q1.C
  N4: LED1.cathode, R1.Pin_1
