# Fritzing sketch RGBLed (saved by Fritzing 0.8.7b)
circuit board: 6.88566cm x 5.36311cm
breadboards: 1

parts:
  Arduino1 = Arduino Uno (Rev3)
  LED1 = RGB LED (com. anode, rbg) [package="5 mm [THT]"]
  R1 = Resistor [tolerance=±5% resistance=100 package=THT]
  R2 = Resistor [tolerance=±5% resistance=150 package=THT]
  R3 = Resistor [tolerance=±5% resistance=150 package=THT]

nets:
  N1: Arduino1.D3_PWM, R1.Pin_0
  N2: Arduino1.D5_PWM, R2.Pin_0
  N3: Arduino1.D6_PWM, R3.Pin_0
  N4: Arduino1.GND, LED1.common_anode
  N5: LED1.red_cathode, R1.Pin_1
  N6: LED1.blue_cathode, R3.Pin_1
  N7: LED1.green_cathode, R2.Pin_1
