# Fritzing sketch mosfet2 (saved by Fritzing 0.8.7b)
circuit board: 6.88566cm x 5.36311cm
breadboards: 1

parts:
  Part1 = Arduino Uno (Rev3)
  R1 = Resistor [tolerance=±5% resistance=100 package=THT]
  Q1 = Basic FET N-Channel [package="TO220 [THT]"]
  Star_LED = Prolight RGB 3 Watt Star
  R2 = Resistor [tolerance=±5% resistance=4.7 package=THT]

nets:
  N1: Part1.D3_PWM, R1.Pin_0
  N2: Part1.5V, Star_LED.B+
  N3: Part1.GND, Q1.source
  N4: R1.Pin_1, Q1.gate
  N5: Q1.drain, R2.Pin_1
  N6: Star_LED.B-, R2.Pin_0
