# Fritzing sketch superflux (saved by Fritzing 0.8.7b)
circuit board: 6.88566cm x 5.36311cm
breadboards: 1

parts:
  Part1 = Arduino Uno (Rev3)
  R1 = Resistor [tolerance=±5% resistance=1k package=THT]
  R2 = Resistor [tolerance=±5% resistance=10 package=THT]
  LED1 = Super Flux LED blue [color=Red]
  Q1 = NPN-Transistor [package="TO92 [THT]"]

nets:
  N1: Part1.D3_PWM, R1.Pin_1
  N2: Part1.5V, LED1.anode
  N3: Part1.GND, Q1.E
  N4: R1.Pin_0, Q1.B
  N5: R2.Pin_0, Q1.C
  N6: R2.Pin_1, LED1.cathode
